# Fritzing sketch WheelwriterBreadboard (saved by Fritzing 0.9.3b)
breadboards: 1

parts:
  R1 = Resistor [tolerance=±5% resistance=200 package=THT]
  Q1 = Basic FET N-Channel [part_number=2n7002 package="TO220 [THT]"]
  Arduino_Nano = Arduino Nano (Rev3.0)
  part = double row female pin header, 10 pins [form="♀ (female)" part_number="IBM Wheelwriter Back Port"]

nets:
  N1: R1.Pin_0, Arduino_Nano.D2
  N2: R1.Pin_1, Q1.gate
  N3: Q1.drain, Arduino_Nano.D3, part.pin5
  N4: Q1.source, Arduino_Nano.GND, part.pin4

notes:
  As seen from the _front_ of the typewriter (e.g., the pins, from left are 5v, 5v, gnd, gnd, bus,...)
